# Fritzing sketch shema (saved by Fritzing 0.9.3b)
breadboards: 1

parts:
  Part1 = Arduino Uno (Rev3)
  Matrix_keypad1 = KEYPAD 4x4
  U1 = LCD-16X2 [package=lcd-8x2]
  SP1 = SPEAKER [package=pcb_mount_speaker]
  PIR1 = PIR sensor
  PIR2 = PIR sensor
  R1 = Resistor [tolerance=±5% resistance=220 package="2010 [SMD]"]

nets:
  N1: Part1.A0, U1.VO
  N2: Part1.A1, U1.DB4
  N3: Part1.A2, U1.DB5
  N4: Part1.A3, U1.DB6
  N5: Part1.A4/SDA, U1.DB7
  N6: Part1.A5/SCL, SP1.+
  N7: Part1.D8, Matrix_keypad1.col2
  N8: Part1.D9_PWM, Matrix_keypad1.col1
  N9: Part1.D10_PWM/SS, PIR1.SIG
  N10: Part1.D11_PWM/MOSI, U1.E
  N11: Part1.D12/MISO, U1.RS
  N12: Part1.D13/SCK, PIR2.SIG
  GND: Part1.GND, U1.VSS, U1.R_W, U1.K, SP1.-, PIR1.GND, PIR2.GND
  N13: Part1.D2, Matrix_keypad1.row4
  N14: Part1.D3_PWM, Matrix_keypad1.row3
  N15: Part1.D4, Matrix_keypad1.row2
  N16: Part1.D5_PWM, Matrix_keypad1.row1
  N17: Part1.D6_PWM, Matrix_keypad1.col4
  N18: Part1.D7, Matrix_keypad1.col3
  VDD: Part1.5V, U1.VDD, PIR1.VDD, PIR2.VDD, R1.Pin_0
  N19: U1.A, R1.Pin_1

custom parts:
  KEYPAD 4x4: Matrix keypad 16 buttons, 4 rows x 4 columns
